# Fritzing sketch skematik breadboard IoT Line Bot arest cloud (saved by Fritzing 0.9.3b)
breadboards: 1

parts:
  R1 = Resistor [tolerance=±5% resistance=220 package=THT]  # not connected
  LED_D1 = LED - 5mm [color="Red (633nm)" package="5 mm [THT]"]
  U1 = NodeMCU V3.0
  RELAY_D2 = Keyes Relay [package=THT]
  MQ-2_A0_SENSOR_GAS = GAS_SENSOR [package=mq-3]
  LAMPU = LEDs [package=led10mm]
  POWER_AC = Power plug

nets:
  N1: LED_D1.cathode, U1.D1
  N2: LED_D1.anode, U1.GND, RELAY_D2.power, MQ-2_A0_SENSOR_GAS.B1
  N3: U1.D2, RELAY_D2.ground
  N4: U1.3V3, U1.VU, RELAY_D2.signal
  N5: U1.EN, MQ-2_A0_SENSOR_GAS.A1
  N6: U1.A0, MQ-2_A0_SENSOR_GAS.H1
  N7: RELAY_D2.C, LAMPU.A
  N8: RELAY_D2.NO, POWER_AC.VCC
  N9: LAMPU.C, POWER_AC.GND

notes:
  hijau = VCC (3.3V/5V)
  coklat = GND
  Design by
  FEBRIAN DWI PUTRA

custom parts:
  NodeMCU V3.0: ESP8266 based NodeMCU
  Keyes Relay: The Keyes 5V relay module is suitable for SCM development, home appliance control. It uses a 5V~12V TIL control signal which can control DC / AC signal.
  LEDs: LEDs Standard schematic elements and footprints for 5mm, 3mm, 1206, and 0603 sized LEDs. 5mm - Spark Fun Electronics SKU : COM-00529 (and others)
